# Fritzing sketch Sistema de riego (saved by Fritzing 0.9.3b)
breadboards: 1

parts:
  Componente1 = Arduino Uno (Rev3) - ICSP
  S1 = Momentary Switch [package=ksa_sealed_tac_switch]
  R1 = Resistor [tolerance=±5% resistance=10k package="0603 [SMD]"]
  WeMos_D1_Mini_Relay_Shield1 = WeMos D1 Mini Relay Shield
  ZS-042_RTC1 = ZS-042 RTC Module

nets:
  N1: Componente1.A4/SDA, ZS-042_RTC1.SDA
  N2: Componente1.A5/SCL, ZS-042_RTC1.SCL
  N3: Componente1.D8, S1.4, R1.Pin_1
  N4: Componente1.D9_PWM, WeMos_D1_Mini_Relay_Shield1.D2
  5V: Componente1.5V, S1.2, WeMos_D1_Mini_Relay_Shield1.5V, ZS-042_RTC1.VCC
  GND: Componente1.GND, R1.Pin_0, WeMos_D1_Mini_Relay_Shield1.G, ZS-042_RTC1.GND
